// Logisim project ALU.circ as structural Verilog: 3 circuits, main circuit ALU
module ALU (
  input  in_1,
  input  [31:0] in_2,
  input  [31:0] in_3,
  input  in_4,
  input  in_5,
  input  in_6,
  input  in_7,
  input  in_8,
  output [31:0] out_9,
  output [31:0] out_10,
  output [31:0] out_11,
  output out_12,
  output out_13,
  output out_14
);

  wire A_B_t_t_t_t, A_B_t_t_t_t_t, A_B_t_t_t_t_t_t, comparator_1_eq, comparator_1_gt, comparator_1_lt,
       comparator_2_eq, comparator_2_gt, comparator_2_lt;
  wire [31:0] A__B, A_B, A_B_t, A_B_t_t, A_B_t_t_t, A_B_t_t_t_t_t_t_t, ALU_Hi_Div, ALU_Hi_Mult, ALU_Lo_Mult,
       AnorB, bit_extender_1_out, bit_extender_2_out, bit_extender_3_out, divider_1_out, divider_1_rem,
       divu_1_out_4, divu_1_out_5, multiplier_1_cout, multiplier_1_out, mulu_1_out_4, mulu_1_out_5;

  Multiplexer #(.width(32), .enable("false")) multiplexer_1 (
    .in0(A_B_t_t_t), .in1(ALU_Lo_Mult), .out(out_11), .sel(in_8));
  Multiplexer #(.width(32), .enable("false")) multiplexer_2 (
    .in0(ALU_Hi_Div), .in1(ALU_Hi_Mult), .out(out_9), .sel(in_8));
  Adder #(.width(32)) adder_1 (.a(in_2), .b(in_3), .out(A_B_t));  // open: cin, cout
  Subtractor #(.width(32)) subtractor_1 (.a(in_2), .b(in_3), .out(A_B_t_t));  // open: bin, bout
  Comparator #(.width(32)) comparator_1 (
    .a(in_2), .b(in_3), .gt(comparator_1_gt), .eq(comparator_1_eq), .lt(comparator_1_lt));
  Comparator #(.width(32), .mode("unsigned")) comparator_2 (
    .a(in_2), .b(in_3), .gt(comparator_2_gt), .eq(comparator_2_eq), .lt(comparator_2_lt));
  assign A_B = in_2 & in_3;  // AND_Gate and_1, 32 bits wide
  assign A__B = in_2 | in_3;  // OR_Gate or_1, 32 bits wide
  assign A_B_t_t_t_t_t_t_t = in_2 ^ in_3;  // XOR_Gate xor_1, 32 bits wide
  assign AnorB = ~(in_2 | in_3);  // NOR_Gate nor_1, 32 bits wide
  Multiplexer #(.enable("false")) multiplexer_3 (
    .in0(comparator_1_gt), .in1(comparator_2_gt), .out(A_B_t_t_t_t_t_t), .sel(in_1));
  assign bit_extender_1_out = {{31{1'b0}}, A_B_t_t_t_t_t};  // Bit_Extender bit_extender_1
  assign bit_extender_2_out = {{31{1'b0}}, A_B_t_t_t_t_t_t};  // Bit_Extender bit_extender_2
  assign bit_extender_3_out = {{31{1'b0}}, A_B_t_t_t_t};  // Bit_Extender bit_extender_3
  and and_2 (A_B_t_t_t_t_t, comparator_1_eq, comparator_2_eq);
  Multiplexer #(.enable("false")) multiplexer_4 (
    .in0(comparator_1_lt), .in1(comparator_2_lt), .out(A_B_t_t_t_t), .sel(in_1));
  DivU divu_1 (.in_2(in_2), .in_3(in_3), .out_4(divu_1_out_4), .out_5(divu_1_out_5), .in_1(in_1));
  Divider #(.width(32)) divider_1 (.a(in_2), .b(in_3), .out(divider_1_out), .rem(divider_1_rem));  // open: upper
  Multiplier #(.width(32)) multiplier_1 (
    .a(in_2), .b(in_3), .out(multiplier_1_out), .cout(multiplier_1_cout));  // open: cin
  MulU mulu_1 (.in_1(in_1), .in_2(in_2), .in_3(in_3), .out_4(mulu_1_out_4), .out_5(mulu_1_out_5));
  Multiplexer_16_main main_1 (
    .in_1(A_B_t), .in_2(A_B_t_t), .in_3(ALU_Lo_Mult), .in_4(A_B_t_t_t), .in_5(bit_extender_1_out),
    .in_6(bit_extender_2_out), .in_7(bit_extender_3_out), .in_8(A_B), .in_9(A__B), .in_10(A_B_t_t_t_t_t_t_t),
    .in_11(AnorB), .in_17({in_7, in_6, in_5, in_4}), .out_18(out_10));  // open: in_12, in_13, in_14, in_15, in_16
  Comparator #(.width(16)) comparator_3 (.a(in_2[15:0]), .b({16{1'b0}}), .gt(out_12), .eq(out_13), .lt(out_14));
  Multiplexer #(.width(32), .enable("false")) multiplexer_5 (
    .in0(divider_1_rem), .in1(divu_1_out_5), .out(ALU_Hi_Div), .sel(in_1));
  Multiplexer #(.width(32), .enable("false")) multiplexer_6 (
    .in0(divider_1_out), .in1(divu_1_out_4), .out(A_B_t_t_t), .sel(in_1));
  Multiplexer #(.width(32), .enable("false")) multiplexer_7 (
    .in0(multiplier_1_out), .in1(mulu_1_out_4), .out(ALU_Lo_Mult), .sel(in_1));
  Multiplexer #(.width(32), .enable("false")) multiplexer_8 (
    .in0(multiplier_1_cout), .in1(mulu_1_out_5), .out(ALU_Hi_Mult), .sel(in_1));

  // Other names for the same wires on the sheet: A[31:0] = in_2; A_0 = out_14; A_0_t = out_13; A_0_t_t = out_12;
  //   ALU_Hi[31:0] = out_9; ALU_Lo[31:0] = out_11; ALU_Lo_Div[31:0] = A_B_t_t_t; AxB[31:0] = ALU_Lo_Mult;
  //   B[31:0] = in_3; N = in_1; Out_ALU[31:0] = out_10; SLoHi = in_8; SA0 = in_4;
  //   SOutALU[3:0] = {in_7, in_6, in_5, in_4}; SA1 = in_5; SA2 = in_6; SA3 = in_7
endmodule

module DivU (
  input  in_1,
  input  [31:0] in_2,
  input  [31:0] in_3,
  output [31:0] out_4,
  output [31:0] out_5
);

  wire and_1_out, and_2_out;
  wire [31:0] multiplexer_1_out, multiplexer_2_out, NegA, NegB;

  Negator #(.width(32)) negator_1 (.in(in_2), .out(NegA));
  Negator #(.width(32)) negator_2 (.in(in_3), .out(NegB));
  Multiplexer #(.width(32), .enable("false")) multiplexer_1 (
    .in0(in_2), .in1(NegA), .out(multiplexer_1_out), .sel(and_1_out));
  and and_1 (and_1_out, in_1, in_2[31]);
  Multiplexer #(.width(32), .enable("false")) multiplexer_2 (
    .in0(in_3), .in1(NegB), .out(multiplexer_2_out), .sel(and_2_out));
  and and_2 (and_2_out, in_3[31], in_1);
  Divider #(.width(32)) divider_1 (
    .a(multiplexer_1_out), .b(multiplexer_2_out), .out(out_4), .rem(out_5));  // open: upper

  // Other names for the same wires on the sheet: A[31:0] = in_2; SignoA = in_2[31]; ADivUB[31:0] = out_4;
  //   B[31:0] = in_3; SignoB = in_3[31]; N = in_1; Resto[31:0] = out_5
endmodule

module MulU (
  input  in_1,
  input  [31:0] in_2,
  input  [31:0] in_3,
  output [31:0] out_4,
  output [31:0] out_5
);

  wire adder_2_cout, not_1_out, Selec, Selec1;
  wire [31:0] adder_1_out, end_Mul_U, end_Up_Mul_U, multiplexer_1_out, multiplexer_2_out, multiplexer_3_out,
       multiplexer_4_out, subtractor_1_out;
  wire [31:2] AMulUB, Resto;
  wire [31:30] Mul, multiplier_1_cout;

  Multiplexer #(.width(32), .enable("false")) multiplexer_1 (
    .in0({1'b0, in_2[31:1]}), .in1(in_2), .out(multiplexer_1_out), .sel(not_1_out));
  not not_1 (not_1_out, in_1);
  Multiplexer #(.width(32), .enable("false")) multiplexer_2 (
    .in0({1'b0, in_3[31:1]}), .in1(in_3), .out(multiplexer_2_out), .sel(not_1_out));
  Multiplier #(.width(32)) multiplier_1 (
    .a(multiplexer_1_out), .b(multiplexer_2_out), .out({Mul, AMulUB}), .cout({multiplier_1_cout, Resto}));  // open: cin
  and and_1 (Selec, in_2[0], in_3[0]);
  or or_1 (Selec1, in_2[0], in_3[0]);
  Subtractor #(.width(32)) subtractor_1 (.a(in_2), .b(32'h1), .out(subtractor_1_out));  // open: bin, bout
  Multiplexer #(.width(32), .enable("false")) multiplexer_3 (
    .in0(in_2), .in1(in_3), .out(multiplexer_3_out), .sel(in_2[0]));
  Adder #(.width(32)) adder_1 (.a(subtractor_1_out), .b(in_3), .out(adder_1_out));  // open: cin, cout
  Multiplexer #(.width(32), .enable("false")) multiplexer_4 (
    .in0(multiplexer_3_out), .in1(adder_1_out), .out(multiplexer_4_out), .sel(Selec));
  Adder #(.width(32)) adder_2 (
    .a(multiplexer_4_out), .b({AMulUB, 2'b00}), .out(end_Mul_U), .cout(adder_2_cout));  // open: cin
  Adder #(.width(32)) adder_3 (.a({Resto, Mul}), .b({32{1'b0}}), .out(end_Up_Mul_U), .cin(adder_2_cout));  // open: cout
  Multiplexer #(.width(32), .enable("false")) multiplexer_5 (
    .in0({AMulUB, 2'b00}), .in1(end_Mul_U), .out(out_4), .sel(Selec1));
  Multiplexer #(.width(32), .enable("false")) multiplexer_6 (
    .in0({Resto, Mul}), .in1(end_Up_Mul_U), .out(out_5), .sel(Selec1));

  // Other names for the same wires on the sheet: _1A = in_2[0]; A[31:0] = in_2; A1[30:0] = in_2[31:1];
  //   Mul[29:0] = AMulUB; _1B = in_3[0]; B[31:0] = in_3; B1[30:0] = in_3[31:1]; Resto[1:0] = Mul; MulU[31:0] = out_4;
  //   MulUHi[31:0] = out_5; N = in_1
endmodule
