// Logisim project BCU.circ as structural Verilog: 1 circuit, main circuit BCU
module BCU (
  input  in_1,
  input  in_2,
  input  in_3,
  input  in_4,
  input  in_5,
  input  [31:0] in_6,
  input  [15:0] in_7,
  input  [25:0] in_8,
  output [31:0] out_9
);

  wire [13:0] I15;
  wire [31:0] adder_1_out, adder_2_out, multiplexer_1_out;

  assign I15 = {{13{1'b0}}, in_7[15]};  // Bit_Extender bit_extender_1
  Adder #(.width(32)) adder_1 (.a(32'h4), .b(out_9), .out(adder_1_out));  // open: cin, cout
  Adder #(.width(32)) adder_2 (.a(adder_1_out), .b({I15, in_7, 2'b00}), .out(adder_2_out));  // open: cin, cout
  Multiplexer #(.select(2), .width(32), .enable("false")) multiplexer_1 (
    .in0(adder_1_out), .in1({out_9[31:28], in_8, 2'b00}), .in2(adder_2_out), .in3(in_6),
    .out(multiplexer_1_out), .sel({in_5, in_4}));
  Register #(.width(32)) register_1 (.D(multiplexer_1_out), .en(in_3), .Q(out_9), .clk(in_1), .clr(in_2));

  // Other names for the same wires on the sheet: OffSet[15:0] = in_7; CLK = in_1; Continue = in_3;
  //   Destino[25:0] = in_8; Destino_Salto[31:2] = {out_9[31:28], in_8}; OPC[31:0] = out_9; RS[31:0] = in_6;
  //   RST = in_2; S0 = in_4; Selector[1:0] = {in_5, in_4}; S1 = in_5
endmodule
