// Logisim project From Ram.circ as structural Verilog: 2 circuits, main circuit main
module main (
  input  CLK,
  input  [3:0] RT,
  input  [31:0] Direccion,
  input  CLR,
  input  START,
  input  [31:0] Banco_0,
  input  [31:0] Banco_1,
  input  [31:0] Banco_2,
  input  [31:0] Banco_3,
  output [15:0] Address,
  output [3:0] MASK,
  output Ready,
  output Chip_Select,
  output [31:0] Instruction_Code
);

  wire demultiplexer_1_out0, \end , Load, or_1_out;
  wire [31:0] main_1_out_18;

  Counter #(.width(4), .max('hf)) counter_1 (
    .load(Load), .D(RT), .count(Chip_Select), .carry(\end ), .clk(CLK));  // open: Q, clr
  or or_1 (or_1_out, demultiplexer_1_out0, START);
  D_Flip_Flop d_ff_1 (.clk(CLK), .D(or_1_out), .Q(Chip_Select), .reset(CLR));  // open: Qn, preset, en
  Multiplexer_16_main main_1 (
    .in_2(Banco_0), .in_3(Banco_1), .in_5(Banco_2), .in_9(Banco_3), .in_17(MASK), .out_18(main_1_out_18));  // open: in_1, in_4, in_6, in_7, in_8, in_10, in_11, in_12, in_13, in_14, in_15, in_16
  Shifter #(.width(4)) shifter_1 (.in(4'b0001), .\dist (Direccion[3:2]), .out(MASK));
  or or_2 (Load, START, Chip_Select);
  Little_Endian little_endian_1 (.IN(main_1_out_18), .OUT(Instruction_Code));
  Demultiplexer demultiplexer_1 (.out0(demultiplexer_1_out0), .out1(Ready), .in(Chip_Select), .sel(\end ));  // open: en

  assign Address = Direccion[19:4];

  // Other names for the same wires on the sheet: Load1 = START; Count = Chip_Select; Load2 = Chip_Select
endmodule

module Little_Endian (
  input  [31:0] IN,
  output [31:0] OUT
);


  assign OUT = {IN[7:0], IN[15:8], IN[23:16], IN[31:24]};
endmodule
