// Logisim project Instruction Decoder.circ as structural Verilog: 1 circuit, main circuit Instruction Decoder
module Instruction_Decoder (
  input  [31:0] Instruction_Code,
  output ADD,
  output SUB,
  output LW,
  output AND,
  output OR,
  output NOT,
  output XOR,
  output SLT,
  output [5:0] Funct_Code,
  output SW,
  output [15:0] K,
  output SLTU,
  output POP,
  output [4:0] RD,
  output TTY,
  output PUSH,
  output RND,
  output [25:0] Destino_Salto,
  output KBD,
  output BLTZ,
  output J,
  output [4:0] RT,
  output BEQ,
  output BNE,
  output [4:0] RS,
  output BLEZ,
  output BGTZ,
  output JR,
  output SLTI,
  output SLTIU,
  output ANDI,
  output ADDI,
  output ORI,
  output XORI,
  output [5:0] OP_Code,
  output MFHI,
  output MFLO,
  output MULT,
  output MULU,
  output DIV,
  output DIVU,
  output NOP,
  output HALT
);

  wire and_4_out, and_5_out, and_6_out, demultiplexer_1_out11, demultiplexer_1_out24, demultiplexer_1_out31,
       demultiplexer_2_out8, FC_KBD, FC_POP, FC_PUSH, FC_RND, FC_TTY, not_1_out, not_2_out, not_3_out,
       OPC____0;
  wire [5:0] multiplexer_1_out;

  and and_1 (FC_POP, ~Instruction_Code[5], ~Instruction_Code[4], ~Instruction_Code[3], ~Instruction_Code[2], ~Instruction_Code[1], ~Instruction_Code[0]);  // AND_Gate
  and and_2 (FC_PUSH, ~Instruction_Code[5], ~Instruction_Code[4], ~Instruction_Code[3], ~Instruction_Code[2], ~Instruction_Code[1], Instruction_Code[0]);  // AND_Gate
  and and_3 (NOP, ~Instruction_Code[0], ~Instruction_Code[1], ~Instruction_Code[2], ~Instruction_Code[3], ~Instruction_Code[4], ~Instruction_Code[5], ~Instruction_Code[6], ~Instruction_Code[7], ~Instruction_Code[8], ~Instruction_Code[9], ~Instruction_Code[10], ~Instruction_Code[11], ~Instruction_Code[12], ~Instruction_Code[13], ~Instruction_Code[14], ~Instruction_Code[15], ~Instruction_Code[16], ~Instruction_Code[17], ~Instruction_Code[18], ~Instruction_Code[19], ~Instruction_Code[20], ~Instruction_Code[21], ~Instruction_Code[22], ~Instruction_Code[23], ~Instruction_Code[24], ~Instruction_Code[25], ~Instruction_Code[26], ~Instruction_Code[27], ~Instruction_Code[28], ~Instruction_Code[29], ~Instruction_Code[30], ~Instruction_Code[31]);  // AND_Gate
  or or_1 (OPC____0, Instruction_Code[26], Instruction_Code[27], Instruction_Code[28], Instruction_Code[29], Instruction_Code[30], Instruction_Code[31]);
  and and_4 (and_4_out, Instruction_Code[0], Instruction_Code[1], Instruction_Code[2], Instruction_Code[3], Instruction_Code[4], Instruction_Code[5]);
  and and_5 (and_5_out, ~Instruction_Code[6], ~Instruction_Code[7], ~Instruction_Code[8], ~Instruction_Code[9], ~Instruction_Code[10], ~Instruction_Code[11], ~Instruction_Code[12], ~Instruction_Code[13], ~Instruction_Code[14], ~Instruction_Code[15], ~Instruction_Code[16], ~Instruction_Code[17], ~Instruction_Code[18], ~Instruction_Code[19], ~Instruction_Code[20], ~Instruction_Code[21], ~Instruction_Code[22], ~Instruction_Code[23], ~Instruction_Code[24], ~Instruction_Code[25]);  // AND_Gate
  and and_6 (and_6_out, Instruction_Code[26], Instruction_Code[27], Instruction_Code[28], Instruction_Code[29], Instruction_Code[30], Instruction_Code[31]);
  and and_7 (FC_TTY, ~Instruction_Code[5], ~Instruction_Code[4], ~Instruction_Code[3], ~Instruction_Code[2], ~Instruction_Code[1], Instruction_Code[0]);  // AND_Gate
  and and_8 (HALT, and_4_out, and_5_out, and_6_out);
  and and_9 (FC_RND, ~Instruction_Code[5], ~Instruction_Code[4], ~Instruction_Code[3], ~Instruction_Code[2], Instruction_Code[1], ~Instruction_Code[0]);  // AND_Gate
  Multiplexer #(.width(6), .enable("false")) multiplexer_1 (
    .in0(Instruction_Code[5:0]), .in1(Instruction_Code[31:26]), .out(multiplexer_1_out), .sel(OPC____0));
  and and_10 (FC_KBD, ~Instruction_Code[5], ~Instruction_Code[4], ~Instruction_Code[3], Instruction_Code[2], ~Instruction_Code[1], ~Instruction_Code[0]);  // AND_Gate
  Demultiplexer #(.select(5)) demultiplexer_1 (
    .out0(ADD), .out2(SUB), .out3(LW), .out4(AND), .out5(OR), .out7(NOT), .out8(XOR), .out10(SLT),
    .out11(demultiplexer_1_out11), .out24(demultiplexer_1_out24), .out31(demultiplexer_1_out31),
    .in(multiplexer_1_out[5]), .sel(multiplexer_1_out[4:0]));  // open: out1, out6, out9, out12, out13, out14, out15, out16, out17, out18, out19, out20, out21, out22, out23, out25, out26, out27, out28, out29, out30, en
  Demultiplexer #(.select(5)) demultiplexer_2 (
    .out1(BLTZ), .out2(J), .out4(BEQ), .out5(BNE), .out6(BLEZ), .out7(BGTZ), .out8(demultiplexer_2_out8),
    .out10(SLTI), .out11(SLTIU), .out12(ANDI), .out13(ORI), .out14(XORI), .out16(MFHI), .out18(MFLO),
    .out24(MULT), .out25(MULU), .out26(DIV), .out27(DIVU), .in(not_1_out), .sel(multiplexer_1_out[4:0]));  // open: out0, out3, out9, out15, out17, out19, out20, out21, out22, out23, out28, out29, out30, out31, en
  not not_1 (not_1_out, multiplexer_1_out[5]);
  not not_2 (not_2_out, OPC____0);
  and and_11 (POP, FC_POP, demultiplexer_1_out24);
  and and_12 (PUSH, demultiplexer_1_out24, FC_PUSH);
  and and_13 (SW, demultiplexer_1_out11, not_2_out);
  and and_14 (SLTU, demultiplexer_1_out11, OPC____0);
  not not_3 (not_3_out, OPC____0);
  and and_15 (JR, demultiplexer_2_out8, not_3_out);
  and and_16 (ADDI, demultiplexer_2_out8, OPC____0);
  and and_17 (TTY, FC_TTY, demultiplexer_1_out31);
  and and_18 (RND, FC_RND, demultiplexer_1_out31);
  and and_19 (KBD, demultiplexer_1_out31, FC_KBD);

  assign Destino_Salto = Instruction_Code[25:0];
  assign Funct_Code = Instruction_Code[5:0];
  assign K = Instruction_Code[15:0];
  assign OP_Code = Instruction_Code[31:26];
  assign RD = Instruction_Code[15:11];
  assign RS = Instruction_Code[25:21];
  assign RT = Instruction_Code[20:16];
endmodule
