// Logisim project Multiplexer 16.circ as structural Verilog: 1 circuit, main circuit main
module main (
  input  [31:0] in_1,
  input  [31:0] in_2,
  input  [31:0] in_3,
  input  [31:0] in_4,
  input  [31:0] in_5,
  input  [31:0] in_6,
  input  [31:0] in_7,
  input  [31:0] in_8,
  input  [31:0] in_9,
  input  [31:0] in_10,
  input  [31:0] in_11,
  input  [31:0] in_12,
  input  [31:0] in_13,
  input  [31:0] in_14,
  input  [31:0] in_15,
  input  [31:0] in_16,
  input  [3:0] in_17,
  output [31:0] out_18
);

  wire decoder_1_out0, decoder_1_out1, decoder_1_out2, decoder_1_out3, decoder_1_out4, decoder_1_out5,
       decoder_1_out6, decoder_1_out7, decoder_1_out8, decoder_1_out9, decoder_1_out10, decoder_1_out11,
       decoder_1_out12, decoder_1_out13, decoder_1_out14, decoder_1_out15;

  Transistor #(.\type ("n"), .gate("br"), .width(32)) transistor_1 (.in(in_1), .out(out_18), .gate(decoder_1_out0));
  Transistor #(.\type ("n"), .gate("br"), .width(32)) transistor_2 (.in(in_2), .out(out_18), .gate(decoder_1_out1));
  Decoder #(.select(4)) decoder_1 (
    .out0(decoder_1_out0), .out1(decoder_1_out1), .out2(decoder_1_out2), .out3(decoder_1_out3),
    .out4(decoder_1_out4), .out5(decoder_1_out5), .out6(decoder_1_out6), .out7(decoder_1_out7),
    .out8(decoder_1_out8), .out9(decoder_1_out9), .out10(decoder_1_out10), .out11(decoder_1_out11),
    .out12(decoder_1_out12), .out13(decoder_1_out13), .out14(decoder_1_out14), .out15(decoder_1_out15),
    .sel(in_17));  // open: en
  Transistor #(.\type ("n"), .gate("br"), .width(32)) transistor_3 (.in(in_3), .out(out_18), .gate(decoder_1_out2));
  Transistor #(.\type ("n"), .gate("br"), .width(32)) transistor_4 (.in(in_4), .out(out_18), .gate(decoder_1_out3));
  Transistor #(.\type ("n"), .gate("br"), .width(32)) transistor_5 (.in(in_5), .out(out_18), .gate(decoder_1_out4));
  Transistor #(.\type ("n"), .gate("br"), .width(32)) transistor_6 (.in(in_6), .out(out_18), .gate(decoder_1_out5));
  Transistor #(.\type ("n"), .gate("br"), .width(32)) transistor_7 (.in(in_7), .out(out_18), .gate(decoder_1_out6));
  Transistor #(.\type ("n"), .gate("br"), .width(32)) transistor_8 (.in(in_8), .out(out_18), .gate(decoder_1_out7));
  Transistor #(.\type ("n"), .gate("br"), .width(32)) transistor_9 (.in(in_9), .out(out_18), .gate(decoder_1_out8));
  Transistor #(.\type ("n"), .gate("br"), .width(32)) transistor_10 (.in(in_10), .out(out_18), .gate(decoder_1_out9));
  Transistor #(.\type ("n"), .gate("br"), .width(32)) transistor_11 (.in(in_11), .out(out_18), .gate(decoder_1_out10));
  Transistor #(.\type ("n"), .gate("br"), .width(32)) transistor_12 (.in(in_12), .out(out_18), .gate(decoder_1_out11));
  Transistor #(.\type ("n"), .gate("br"), .width(32)) transistor_13 (.in(in_13), .out(out_18), .gate(decoder_1_out12));
  Transistor #(.\type ("n"), .gate("br"), .width(32)) transistor_14 (.in(in_14), .out(out_18), .gate(decoder_1_out13));
  Transistor #(.\type ("n"), .gate("br"), .width(32)) transistor_15 (.in(in_15), .out(out_18), .gate(decoder_1_out14));
  Transistor #(.\type ("n"), .gate("br"), .width(32)) transistor_16 (.in(in_16), .out(out_18), .gate(decoder_1_out15));
endmodule
