// Logisim project Multiplexer 32.circ as structural Verilog: 1 circuit, main circuit main
module main (
  input  [31:0] Input_0,
  input  [31:0] Input_1,
  input  [31:0] Input_2,
  input  [31:0] Input_3,
  input  [31:0] Input_4,
  input  [31:0] Input_5,
  input  [31:0] Input_6,
  input  [31:0] Input_7,
  input  [31:0] Input_8,
  input  [31:0] Input_9,
  input  [31:0] Input_10,
  input  [31:0] Input_11,
  input  [31:0] Input_12,
  input  [31:0] Input_13,
  input  [31:0] Input_14,
  input  [31:0] Input_15,
  input  [31:0] Input_16,
  input  [31:0] Input_17,
  input  [31:0] Input_18,
  input  [31:0] Input_19,
  input  [31:0] Input_20,
  input  [31:0] Input_21,
  input  [31:0] Input_22,
  input  [31:0] Input_23,
  input  [31:0] Input_24,
  input  [31:0] Input_25,
  input  [31:0] Input_26,
  input  [31:0] Input_27,
  input  [31:0] Input_28,
  input  [31:0] Input_29,
  input  [31:0] Input_30,
  input  [31:0] Input_31,
  input  [4:0] Selector,
  output [31:0] Output
);

  wire decoder_1_out0, decoder_1_out1, decoder_1_out2, decoder_1_out3, decoder_1_out4, decoder_1_out5,
       decoder_1_out6, decoder_1_out7, decoder_1_out8, decoder_1_out9, decoder_1_out10, decoder_1_out11,
       decoder_1_out12, decoder_1_out13, decoder_1_out14, decoder_1_out15, decoder_1_out16, decoder_1_out17,
       decoder_1_out18, decoder_1_out19, decoder_1_out20, decoder_1_out21, decoder_1_out22, decoder_1_out23,
       decoder_1_out24, decoder_1_out25, decoder_1_out26, decoder_1_out27, decoder_1_out28, decoder_1_out29,
       decoder_1_out30, decoder_1_out31;

  Transistor #(.\type ("n"), .gate("br"), .width(32)) transistor_1 (.in(Input_0), .out(Output), .gate(decoder_1_out0));
  Transistor #(.\type ("n"), .gate("br"), .width(32)) transistor_2 (.in(Input_1), .out(Output), .gate(decoder_1_out1));
  Transistor #(.\type ("n"), .gate("br"), .width(32)) transistor_3 (.in(Input_2), .out(Output), .gate(decoder_1_out2));
  Decoder #(.select(5)) decoder_1 (
    .out0(decoder_1_out0), .out1(decoder_1_out1), .out2(decoder_1_out2), .out3(decoder_1_out3),
    .out4(decoder_1_out4), .out5(decoder_1_out5), .out6(decoder_1_out6), .out7(decoder_1_out7),
    .out8(decoder_1_out8), .out9(decoder_1_out9), .out10(decoder_1_out10), .out11(decoder_1_out11),
    .out12(decoder_1_out12), .out13(decoder_1_out13), .out14(decoder_1_out14), .out15(decoder_1_out15),
    .out16(decoder_1_out16), .out17(decoder_1_out17), .out18(decoder_1_out18), .out19(decoder_1_out19),
    .out20(decoder_1_out20), .out21(decoder_1_out21), .out22(decoder_1_out22), .out23(decoder_1_out23),
    .out24(decoder_1_out24), .out25(decoder_1_out25), .out26(decoder_1_out26), .out27(decoder_1_out27),
    .out28(decoder_1_out28), .out29(decoder_1_out29), .out30(decoder_1_out30), .out31(decoder_1_out31),
    .sel(Selector));  // open: en
  Transistor #(.\type ("n"), .gate("br"), .width(32)) transistor_4 (.in(Input_3), .out(Output), .gate(decoder_1_out3));
  Transistor #(.\type ("n"), .gate("br"), .width(32)) transistor_5 (.in(Input_4), .out(Output), .gate(decoder_1_out4));
  Transistor #(.\type ("n"), .gate("br"), .width(32)) transistor_6 (.in(Input_5), .out(Output), .gate(decoder_1_out5));
  Transistor #(.\type ("n"), .gate("br"), .width(32)) transistor_7 (.in(Input_6), .out(Output), .gate(decoder_1_out6));
  Transistor #(.\type ("n"), .gate("br"), .width(32)) transistor_8 (.in(Input_7), .out(Output), .gate(decoder_1_out7));
  Transistor #(.\type ("n"), .gate("br"), .width(32)) transistor_9 (.in(Input_8), .out(Output), .gate(decoder_1_out8));
  Transistor #(.\type ("n"), .gate("br"), .width(32)) transistor_10 (.in(Input_9), .out(Output), .gate(decoder_1_out9));
  Transistor #(.\type ("n"), .gate("br"), .width(32)) transistor_11 (
    .in(Input_10), .out(Output), .gate(decoder_1_out10));
  Transistor #(.\type ("n"), .gate("br"), .width(32)) transistor_12 (
    .in(Input_11), .out(Output), .gate(decoder_1_out11));
  Transistor #(.\type ("n"), .gate("br"), .width(32)) transistor_13 (
    .in(Input_12), .out(Output), .gate(decoder_1_out12));
  Transistor #(.\type ("n"), .gate("br"), .width(32)) transistor_14 (
    .in(Input_13), .out(Output), .gate(decoder_1_out13));
  Transistor #(.\type ("n"), .gate("br"), .width(32)) transistor_15 (
    .in(Input_14), .out(Output), .gate(decoder_1_out14));
  Transistor #(.\type ("n"), .gate("br"), .width(32)) transistor_16 (
    .in(Input_15), .out(Output), .gate(decoder_1_out15));
  Transistor #(.\type ("n"), .gate("br"), .width(32)) transistor_17 (
    .in(Input_16), .out(Output), .gate(decoder_1_out16));
  Transistor #(.\type ("n"), .gate("br"), .width(32)) transistor_18 (
    .in(Input_17), .out(Output), .gate(decoder_1_out17));
  Transistor #(.\type ("n"), .gate("br"), .width(32)) transistor_19 (
    .in(Input_18), .out(Output), .gate(decoder_1_out18));
  Transistor #(.\type ("n"), .gate("br"), .width(32)) transistor_20 (
    .in(Input_19), .out(Output), .gate(decoder_1_out19));
  Transistor #(.\type ("n"), .gate("br"), .width(32)) transistor_21 (
    .in(Input_20), .out(Output), .gate(decoder_1_out20));
  Transistor #(.\type ("n"), .gate("br"), .width(32)) transistor_22 (
    .in(Input_21), .out(Output), .gate(decoder_1_out21));
  Transistor #(.\type ("n"), .gate("br"), .width(32)) transistor_23 (
    .in(Input_22), .out(Output), .gate(decoder_1_out22));
  Transistor #(.\type ("n"), .gate("br"), .width(32)) transistor_24 (
    .in(Input_23), .out(Output), .gate(decoder_1_out23));
  Transistor #(.\type ("n"), .gate("br"), .width(32)) transistor_25 (
    .in(Input_24), .out(Output), .gate(decoder_1_out24));
  Transistor #(.\type ("n"), .gate("br"), .width(32)) transistor_26 (
    .in(Input_25), .out(Output), .gate(decoder_1_out25));
  Transistor #(.\type ("n"), .gate("br"), .width(32)) transistor_27 (
    .in(Input_26), .out(Output), .gate(decoder_1_out26));
  Transistor #(.\type ("n"), .gate("br"), .width(32)) transistor_28 (
    .in(Input_27), .out(Output), .gate(decoder_1_out27));
  Transistor #(.\type ("n"), .gate("br"), .width(32)) transistor_29 (
    .in(Input_28), .out(Output), .gate(decoder_1_out28));
  Transistor #(.\type ("n"), .gate("br"), .width(32)) transistor_30 (
    .in(Input_29), .out(Output), .gate(decoder_1_out29));
  Transistor #(.\type ("n"), .gate("br"), .width(32)) transistor_31 (
    .in(Input_30), .out(Output), .gate(decoder_1_out30));
  Transistor #(.\type ("n"), .gate("br"), .width(32)) transistor_32 (
    .in(Input_31), .out(Output), .gate(decoder_1_out31));
endmodule
