// Logisim project RegisterFile.circ as structural Verilog: 1 circuit, main circuit RegisterFile
module RegisterFile (
  input  [31:0] in_1,
  input  [31:0] in_2,
  input  [31:0] in_3,
  input  [31:0] in_4,
  input  [31:0] in_5,
  input  [31:0] in_6,
  input  in_7,
  input  in_8,
  input  in_9,
  input  in_10,
  input  in_11,
  input  in_12,
  input  in_13,
  input  in_14,
  input  [4:0] in_15,
  input  [4:0] in_16,
  input  [4:0] in_17,
  input  in_18,
  input  in_19,
  input  in_20,
  input  in_21,
  input  [31:0] in_22,
  input  [31:0] in_23,
  output [31:0] out_24,
  output [31:0] out_25,
  output [31:0] out_26,
  output [31:0] out_27,
  output [31:0] out_28,
  output [31:0] out_29,
  output [31:0] out_30
);

  wire Enable_R0, Enable_R1, Enable_R2, Enable_R3, Enable_R4, Enable_R5, Enable_R6, Enable_R7, Enable_R8,
       Enable_R9, Enable_R10, Enable_R11, Enable_R12, Enable_R13, Enable_R14, Enable_R15, Enable_R16,
       Enable_R17, Enable_R18, Enable_R19, Enable_R20, Enable_R21, Enable_R22, Enable_R23, Enable_R24,
       Enable_R25, Enable_R26, Enable_R27, Enable_R28, Enable_R29, Enable_R30, Enable_R31, or_1_out;
  wire [4:0] multiplexer_1_out;
  wire [31:0] D, multiplexer_2_out, multiplexer_3_out, Out_R0, Out_R1, Out_R2, Out_R3, Out_R4, Out_R5,
       Out_R6, Out_R7, Out_R8, Out_R9, Out_R10, Out_R11, Out_R12, Out_R13, Out_R14, Out_R15, Out_R16,
       Out_R17, Out_R18, Out_R19, Out_R20, Out_R21, Out_R22, Out_R23, Out_R24, Out_R25, Out_R26, Out_R27,
       Out_R28, Out_R29, Out_R30;

  Demultiplexer #(.select(5), .enable("false")) demultiplexer_1 (
    .out0(Enable_R0), .out1(Enable_R1), .out2(Enable_R2), .out3(Enable_R3), .out4(Enable_R4),
    .out5(Enable_R5), .out6(Enable_R6), .out7(Enable_R7), .out8(Enable_R8), .out9(Enable_R9),
    .out10(Enable_R10), .out11(Enable_R11), .out12(Enable_R12), .out13(Enable_R13), .out14(Enable_R14),
    .out15(Enable_R15), .out16(Enable_R16), .out17(Enable_R17), .out18(Enable_R18), .out19(Enable_R19),
    .out20(Enable_R20), .out21(Enable_R21), .out22(Enable_R22), .out23(Enable_R23), .out24(Enable_R24),
    .out25(Enable_R25), .out26(Enable_R26), .out27(Enable_R27), .out28(Enable_R28), .out29(Enable_R29),
    .out30(Enable_R30), .out31(Enable_R31), .in(in_9), .sel(multiplexer_1_out));
  Multiplexer #(.width(5), .enable("false")) multiplexer_1 (
    .in0(in_17), .in1(in_16), .out(multiplexer_1_out), .sel(in_18));
  Multiplexer_8_main main_1 (
    .in_1(in_1), .in_2(in_4), .in_3(out_29), .in_4(out_28), .in_5(in_2), .in_6(in_3), .in_7(in_23),
    .in_8(in_22), .in_9({in_14, in_13, in_12}), .out_10(D));
  Multiplexer_32_main main_2 (
    .Input_0(Out_R0), .Input_1(Out_R1), .Input_2(Out_R2), .Input_3(Out_R3), .Input_4(Out_R4),
    .Input_5(Out_R5), .Input_6(Out_R6), .Input_7(Out_R7), .Input_8(Out_R8), .Input_9(Out_R9),
    .Input_10(Out_R10), .Input_11(Out_R11), .Input_12(Out_R12), .Input_13(Out_R13), .Input_14(Out_R14),
    .Input_15(Out_R15), .Input_16(Out_R16), .Input_17(Out_R17), .Input_18(Out_R18), .Input_19(Out_R19),
    .Input_20(Out_R20), .Input_21(Out_R21), .Input_22(Out_R22), .Input_23(Out_R23), .Input_24(Out_R24),
    .Input_25(Out_R25), .Input_26(Out_R26), .Input_27(Out_R27), .Input_28(Out_R28), .Input_29(Out_R29),
    .Input_30(Out_R30), .Input_31(out_30), .Selector(in_15), .Output(out_24));
  Register #(.width(32)) Hi (.D(in_5), .en(in_10), .Q(out_28), .clk(in_7), .clr(in_8));
  Register #(.width(32)) Lo (.D(in_6), .en(in_11), .Q(out_29), .clk(in_7), .clr(in_8));
  Register #(.width(32)) R0 (.D(D), .en(Enable_R0), .Q(Out_R0), .clk(in_7), .clr(in_8));
  Register #(.width(32)) R1 (.D(D), .en(Enable_R1), .Q(Out_R1), .clk(in_7), .clr(in_8));
  Register #(.width(32)) R2 (.D(D), .en(Enable_R2), .Q(Out_R2), .clk(in_7), .clr(in_8));
  Register #(.width(32)) R3 (.D(D), .en(Enable_R3), .Q(Out_R3), .clk(in_7), .clr(in_8));
  Multiplexer_32_main main_3 (
    .Input_0(Out_R0), .Input_1(Out_R1), .Input_2(Out_R2), .Input_3(Out_R3), .Input_4(Out_R4),
    .Input_5(Out_R5), .Input_6(Out_R6), .Input_7(Out_R7), .Input_8(Out_R8), .Input_9(Out_R9),
    .Input_10(Out_R10), .Input_11(Out_R11), .Input_12(Out_R12), .Input_13(Out_R13), .Input_14(Out_R14),
    .Input_15(Out_R15), .Input_16(Out_R16), .Input_17(Out_R17), .Input_18(Out_R18), .Input_19(Out_R19),
    .Input_20(Out_R20), .Input_21(Out_R21), .Input_22(Out_R22), .Input_23(Out_R23), .Input_24(Out_R24),
    .Input_25(Out_R25), .Input_26(Out_R26), .Input_27(Out_R27), .Input_28(Out_R28), .Input_29(Out_R29),
    .Input_30(Out_R30), .Input_31(out_30), .Selector(in_16), .Output(out_25));
  Register #(.width(32)) R4 (.D(D), .en(Enable_R4), .Q(Out_R4), .clk(in_7), .clr(in_8));
  Register #(.width(32)) R5 (.D(D), .en(Enable_R5), .Q(Out_R5), .clk(in_7), .clr(in_8));
  Register #(.width(32)) R6 (.D(D), .en(Enable_R6), .Q(Out_R6), .clk(in_7), .clr(in_8));
  Register #(.width(32)) R7 (.D(D), .en(Enable_R7), .Q(Out_R7), .clk(in_7), .clr(in_8));
  Register #(.width(32)) R8 (.D(D), .en(Enable_R8), .Q(Out_R8), .clk(in_7), .clr(in_8));
  Register #(.width(32)) R9 (.D(D), .en(Enable_R9), .Q(Out_R9), .clk(in_7), .clr(in_8));
  Register #(.width(32)) R10 (.D(D), .en(Enable_R10), .Q(Out_R10), .clk(in_7), .clr(in_8));
  Register #(.width(32)) R11 (.D(D), .en(Enable_R11), .Q(Out_R11), .clk(in_7), .clr(in_8));
  Register #(.width(32)) R12 (.D(D), .en(Enable_R12), .Q(Out_R12), .clk(in_7), .clr(in_8));
  Register #(.width(32)) R13 (.D(D), .en(Enable_R13), .Q(Out_R13), .clk(in_7), .clr(in_8));
  Register #(.width(32)) R14 (.D(D), .en(Enable_R14), .Q(Out_R14), .clk(in_7), .clr(in_8));
  Register #(.width(32)) R15 (.D(D), .en(Enable_R15), .Q(Out_R15), .clk(in_7), .clr(in_8));
  Register #(.width(32)) R16 (.D(D), .en(Enable_R16), .Q(Out_R16), .clk(in_7), .clr(in_8));
  Register #(.width(32)) R17 (.D(D), .en(Enable_R17), .Q(Out_R17), .clk(in_7), .clr(in_8));
  Register #(.width(32)) R18 (.D(D), .en(Enable_R18), .Q(Out_R18), .clk(in_7), .clr(in_8));
  Register #(.width(32)) R19 (.D(D), .en(Enable_R19), .Q(Out_R19), .clk(in_7), .clr(in_8));
  Register #(.width(32)) R20 (.D(D), .en(Enable_R20), .Q(Out_R20), .clk(in_7), .clr(in_8));
  Register #(.width(32)) R21 (.D(D), .en(Enable_R21), .Q(Out_R21), .clk(in_7), .clr(in_8));
  Register #(.width(32)) R22 (.D(D), .en(Enable_R22), .Q(Out_R22), .clk(in_7), .clr(in_8));
  Register #(.width(32)) R23 (.D(D), .en(Enable_R23), .Q(Out_R23), .clk(in_7), .clr(in_8));
  Register #(.width(32)) R24 (.D(D), .en(Enable_R24), .Q(Out_R24), .clk(in_7), .clr(in_8));
  Register #(.width(32)) R25 (.D(D), .en(Enable_R25), .Q(Out_R25), .clk(in_7), .clr(in_8));
  Register #(.width(32)) R26 (.D(D), .en(Enable_R26), .Q(Out_R26), .clk(in_7), .clr(in_8));
  Register #(.width(32)) R27 (.D(D), .en(Enable_R27), .Q(Out_R27), .clk(in_7), .clr(in_8));
  Register #(.width(32)) R28 (.D(D), .en(Enable_R28), .Q(Out_R28), .clk(in_7), .clr(in_8));
  Register #(.width(32)) R29 (.D(D), .en(Enable_R29), .Q(Out_R29), .clk(in_7), .clr(in_8));
  Register #(.width(32)) R30 (.D(D), .en(Enable_R30), .Q(Out_R30), .clk(in_7), .clr(in_8));
  Multiplexer #(.width(32), .enable("false")) multiplexer_2 (
    .in0(out_30), .in1(32'hfffc), .out(multiplexer_2_out), .sel(in_8));
  Multiplexer #(.select(2), .width(32), .enable("false")) multiplexer_3 (
    .in0(multiplexer_2_out), .in1(in_3), .in2(in_2), .out(multiplexer_3_out), .sel({in_20, in_19}));  // open: in3
  or or_1 (or_1_out, Enable_R31, in_8, in_21);
  Register #(.width(32)) R31 (.D(multiplexer_3_out), .en(or_1_out), .Q(out_30), .clk(in_7));  // open: clr
  Adder #(.width(32)) adder_1 (.a(out_30), .b(32'h4), .out(out_26));  // open: cin, cout
  Subtractor #(.width(32)) subtractor_1 (.a(out_30), .b(32'h4), .out(out_27));  // open: bin, bout

  // Other names for the same wires on the sheet: S0SP = in_19; S1SP = in_20; ALU[31:0] = in_1; CLK = in_7;
  //   D_Hi[31:0] = in_5; D_Lo[31:0] = in_6; En_Hi = in_10; En_Lo = in_11; Enable = in_9; EnableSP = in_21;
  //   Kbd[31:0] = in_22; Out_Hi[31:0] = out_28; Out_Lo[31:0] = out_29; Out_RS[31:0] = out_24; Out_RT[31:0] = out_25;
  //   Out_SP[31:0] = out_30; Out_SP_4[31:0] = out_26; Out_SP_4_t[31:0] = out_27; RAM[31:0] = in_4; RD[4:0] = in_17;
  //   Rnd[31:0] = in_23; RS[4:0] = in_15; RST = in_8; RT[4:0] = in_16; SD0 = in_12;
  //   Selector_D[2:0] = {in_14, in_13, in_12}; SD1 = in_13; SD2 = in_14; SelectorR = in_18; SP_4[31:0] = in_3;
  //   SP_4_t[31:0] = in_2
endmodule
