// Logisim project s-mips.circ as structural Verilog: 5 circuits, main circuit S-MIPS Board
module S_MIPS_Board (
  output halt
);

  wire button_1_out, CLK, CS, d_ff_1_q, R_W, Reset_out, RST, TTY_EN;
  wire [2:0] KDB;
  wire [3:0] Mask, ram_1_read_time, ram_1_write_time;
  wire [6:0] KDB_DATA, TTY_DATA;
  wire [15:0] Addr;
  wire [31:0] ram_1_data_out_0, ram_1_data_out_1, ram_1_data_out_2, ram_1_data_out_3, s_mips_1_ram_in_0,
       s_mips_1_ram_in_1, s_mips_1_ram_in_2, s_mips_1_ram_in_3;

  TTY #(.rows(25), .cols(80)) tty_1 (.data(TTY_DATA), .clk(CLK), .we(TTY_EN), .clr(RST));
  RAM ram_1 (
    .Address(Addr), .Data_Out_0(ram_1_data_out_0), .Data_Out_1(ram_1_data_out_1),
    .Data_Out_2(ram_1_data_out_2), .Data_Out_3(ram_1_data_out_3), .Data_In_0(s_mips_1_ram_in_0),
    .Data_In_1(s_mips_1_ram_in_1), .Data_In_2(s_mips_1_ram_in_2), .Data_In_3(s_mips_1_ram_in_3), .Mask(Mask),
    .nRead_Write(R_W), .Chip_Select(CS), .Read_Time(ram_1_read_time), .Reset(button_1_out),
    .Write_Time(ram_1_write_time));
  Button button_1 (.out(button_1_out));
  Keyboard #(.buflen(64)) keyboard_1 (.clk(CLK), .re(KDB[0]), .avail(KDB[2]), .data(KDB_DATA));  // open: clr
  S_MIPS s_mips_1 (
    .Kbd_Enable(KDB[0]), .Address(Addr), .Kbd_Clear(KDB[1]), .Kbd_Available(KDB[2]),
    .RAM_In_0(s_mips_1_ram_in_0), .Kbd_ASCII_Data(KDB_DATA), .RAM_In_1(s_mips_1_ram_in_1),
    .TTY_Enable(TTY_EN), .RAM_In_2(s_mips_1_ram_in_2), .RAM_In_3(s_mips_1_ram_in_3),
    .TTY_ASCII_Data(TTY_DATA), .Reset(RST), .RAM_Out_0(ram_1_data_out_0), .Clock(CLK),
    .RAM_Out_1(ram_1_data_out_1), .Stop(halt), .RAM_Out_2(ram_1_data_out_2), .RAM_Out_3(ram_1_data_out_3),
    .Mask(Mask), .Read_Time(ram_1_read_time), .Write_Time(ram_1_write_time), .nRead_Write(R_W),
    .Chip_Select(CS));
  D_Flip_Flop d_ff_1 (.clk(CLK), .D(1'b1), .Q(d_ff_1_q), .reset(Reset_out));  // open: Qn, preset, en
  Button Reset (.out(Reset_out));
  Clock clock_1 (.out(CLK));
  D_Flip_Flop d_ff_2 (.clk(CLK), .D(d_ff_1_q), .Qn(RST), .reset(Reset_out));  // open: Q, preset, en

  // Notes on the sheet:
  //   NO MODIFICAR
  //   Keyboard
endmodule

module RAM (
  input  [15:0] Address,
  input  [31:0] Data_In_0,
  input  [31:0] Data_In_1,
  input  [31:0] Data_In_2,
  input  [31:0] Data_In_3,
  input  [3:0] Mask,
  input  nRead_Write,
  input  Chip_Select,
  input  Reset,
  output [31:0] Data_Out_0,
  output [31:0] Data_Out_1,
  output [31:0] Data_Out_2,
  output [31:0] Data_Out_3,
  output [3:0] Read_Time,
  output [3:0] Write_Time
);

  wire and_2_out, and_3_out, and_4_out, and_5_out, and_6_out, and_7_out, and_8_out, and_9_out, Changed, CLK,
       comparator_2_eq, comparator_3_eq, comparator_4_eq, comparator_5_eq, comparator_6_eq, Count,
       demultiplexer_3_out0, Idle, Idle_q, Load, Load0, Load1, nand_1_out, or_1_out, or_2_out, or_3_out,
       or_4_out, or_5_out, or_6_out, or_7_out, or_8_out, or_9_out, or_10_out, Proc_q, Update_Mem, Zero_Time;
  wire [3:0] counter_1_q, multiplexer_1_out, subtractor_1_out;
  wire [31:0] register_1_q, register_2_q, register_3_q, register_4_q, register_5_q;

  // Probe on 4'b0011
  // Probe on 4'b0101
  Multiplexer #(.width(4), .enable("false")) multiplexer_1 (
    .in0(4'b0011), .in1(4'b0101), .out(multiplexer_1_out), .sel(nRead_Write));
  or or_1 (or_1_out, Idle, Update_Mem);
  or or_2 (or_2_out, ~Chip_Select, Reset);  // OR_Gate
  Subtractor #(.width(4)) subtractor_1 (.a(multiplexer_1_out), .b(4'b0010), .out(subtractor_1_out));  // open: bin, bout
  Demultiplexer #(.enable("false")) demultiplexer_1 (.out0(Idle), .out1(Load0), .in(Idle_q), .sel(Changed));
  D_Flip_Flop u_Idle (.clk(CLK), .D(or_1_out), .Q(Idle_q), .preset(or_2_out));  // open: Qn, en, reset
  // Probe on counter_1_q
  Counter #(.width(4), .max('hf)) counter_1 (
    .load(Load), .D(subtractor_1_out), .count(Count), .Q(counter_1_q), .clk(CLK), .clr(or_3_out));  // open: carry
  or or_3 (or_3_out, ~Chip_Select, Reset);  // OR_Gate
  Comparator #(.width(4), .mode("unsigned")) comparator_1 (
    .a(4'b0000), .b(counter_1_q), .eq(Zero_Time));  // open: gt, lt
  or or_4 (or_4_out, Count, Load0, Load1);
  Register #(.width(32)) register_1 (.D(Data_In_0), .en(Chip_Select), .Q(register_1_q), .clk(CLK), .clr(or_5_out));
  or or_5 (or_5_out, ~Chip_Select, Reset);  // OR_Gate
  Register #(.width(32)) register_2 (.D(Data_In_1), .en(Chip_Select), .Q(register_2_q), .clk(CLK), .clr(or_6_out));
  or or_6 (or_6_out, ~Chip_Select, Reset);  // OR_Gate
  Register #(.width(32)) register_3 (.D(Data_In_2), .en(Chip_Select), .Q(register_3_q), .clk(CLK), .clr(or_7_out));
  or or_7 (or_7_out, ~Chip_Select, Reset);  // OR_Gate
  Register #(.width(32)) register_4 (.D(Data_In_3), .en(Chip_Select), .Q(register_4_q), .clk(CLK), .clr(or_8_out));
  or or_8 (or_8_out, ~Chip_Select, Reset);  // OR_Gate
  Register #(.width(32)) register_5 (
    .D({{11{1'b1}}, nRead_Write, Mask, Address}), .en(Chip_Select), .Q(register_5_q), .clk(CLK),
    .clr(or_9_out));
  or or_9 (or_9_out, ~Chip_Select, Reset);  // OR_Gate
  D_Flip_Flop Proc (.clk(CLK), .D(or_4_out), .Q(Proc_q), .reset(or_10_out));  // open: Qn, preset, en
  or or_10 (or_10_out, ~Chip_Select, Reset);  // OR_Gate
  Demultiplexer #(.enable("false")) demultiplexer_2 (
    .out0(Count), .out1(Update_Mem), .in(demultiplexer_3_out0), .sel(Zero_Time));
  Demultiplexer #(.enable("false")) demultiplexer_3 (
    .out0(demultiplexer_3_out0), .out1(Load1), .in(Proc_q), .sel(Changed));
  Clock clock_1 (.out(CLK));
  Comparator #(.width(32)) comparator_2 (.a(register_1_q), .b(Data_In_0), .eq(comparator_2_eq));  // open: gt, lt
  Comparator #(.width(32)) comparator_3 (.a(register_2_q), .b(Data_In_1), .eq(comparator_3_eq));  // open: gt, lt
  Comparator #(.width(32)) comparator_4 (.a(register_3_q), .b(Data_In_2), .eq(comparator_4_eq));  // open: gt, lt
  Comparator #(.width(32)) comparator_5 (.a(register_4_q), .b(Data_In_3), .eq(comparator_5_eq));  // open: gt, lt
  Comparator #(.width(32)) comparator_6 (
    .a(register_5_q), .b({{11{1'b1}}, nRead_Write, Mask, Address}), .eq(comparator_6_eq));  // open: gt, lt
  nand nand_1 (nand_1_out, comparator_6_eq, comparator_2_eq, comparator_3_eq, comparator_4_eq, comparator_5_eq);
  and and_1 (Changed, nand_1_out, Chip_Select);
  or or_11 (Load, Count, Load1, Load0);
  and and_2 (and_2_out, Mask[0], Update_Mem, nRead_Write);
  and and_3 (and_3_out, Mask[1], Update_Mem, nRead_Write);
  and and_4 (and_4_out, Mask[2], Update_Mem, nRead_Write);
  and and_5 (and_5_out, Mask[3], Update_Mem, nRead_Write);
  RAM_part #(.addrWidth(16), .dataWidth(32), .bus("separate")) ram_1 (
    .addr(Address), .din(Data_In_0), .data(Data_Out_0), .str(and_2_out), .sel(Chip_Select), .clk(CLK),
    .ld(and_6_out), .clr(Reset));
  and and_6 (and_6_out, ~nRead_Write, Idle);  // AND_Gate
  RAM_part #(.addrWidth(16), .dataWidth(32), .bus("separate")) ram_2 (
    .addr(Address), .din(Data_In_1), .data(Data_Out_1), .str(and_3_out), .sel(Chip_Select), .clk(CLK),
    .ld(and_7_out), .clr(Reset));
  and and_7 (and_7_out, ~nRead_Write, Idle);  // AND_Gate
  RAM_part #(.addrWidth(16), .dataWidth(32), .bus("separate")) ram_3 (
    .addr(Address), .din(Data_In_2), .data(Data_Out_2), .str(and_4_out), .sel(Chip_Select), .clk(CLK),
    .ld(and_8_out), .clr(Reset));
  and and_8 (and_8_out, ~nRead_Write, Idle);  // AND_Gate
  RAM_part #(.addrWidth(16), .dataWidth(32), .bus("separate")) ram_4 (
    .addr(Address), .din(Data_In_3), .data(Data_Out_3), .str(and_5_out), .sel(Chip_Select), .clk(CLK),
    .ld(and_9_out), .clr(Reset));
  and and_9 (and_9_out, ~nRead_Write, Idle);  // AND_Gate

  assign Read_Time = 4'b0011;
  assign Write_Time = 4'b0101;

  // Other names for the same wires on the sheet: M0 = Mask[0]; M1 = Mask[1]; M2 = Mask[2]; M3 = Mask[3];
  //   RW = nRead_Write; CLR = Reset; CS = Chip_Select; Load2 = Count

  // Notes on the sheet:
  //   NO MODIFICAR
  //   excepto quizás los valores RT y WT
  //   BANK0
  //   BANK1
  //   BANK2
  //   BANK3
endmodule

module S_MIPS (
  input  Kbd_Available,
  input  [6:0] Kbd_ASCII_Data,
  input  [31:0] RAM_Out_0,
  input  [31:0] RAM_Out_1,
  input  Reset,
  input  [31:0] RAM_Out_2,
  input  Clock,
  input  [31:0] RAM_Out_3,
  input  [3:0] Read_Time,
  input  [3:0] Write_Time,
  output Kbd_Enable,
  output [15:0] Address,
  output Kbd_Clear,
  output TTY_Enable,
  output [6:0] TTY_ASCII_Data,
  output Stop,
  output [31:0] RAM_In_0,
  output [31:0] RAM_In_1,
  output [31:0] RAM_In_2,
  output [31:0] RAM_In_3,
  output [3:0] Mask,
  output nRead_Write,
  output Chip_Select
);

  wire A_0, A_0_t, A_0_t_t, add, addi, \and , and_28_out, and_29_out, and_30_out, and_36_out, andi,
       B_Selector, beq, bgtz, blez, bltz, bne, BSelector_Addi, BSelector_Andi, BSelector_Lw, BSelector_Lw0,
       BSelector_Lw1, BSelector_Ori, BSelector_Slti, BSelector_Sltiu, BSelector_Sltu, BSelector_Sw,
       BSelector_Sw0, BSelector_Sw1, BSelector_Xori, Cont, Cont_Add, Cont_And, Cont_Beq, Cont_Bgtz,
       Cont_Blez, Cont_Bltz, Cont_Bne, Cont_Div, Cont_Divu, Cont_J, Cont_Jr, Cont_Lw, Cont_Mfhi, Cont_Mflo,
       Cont_Mult, Cont_Mulu, Cont_Nop, Cont_Nor, Cont_Or, Cont_Pop, Cont_Push, Cont_Rnd, Cont_Slt, Cont_Sub,
       Cont_Sw, Cont_Xor, CS0, CS2, CS4, demultiplexer_1_out1, demultiplexer_2_out0, demultiplexer_3_out0,
       demultiplexer_4_out0, demultiplexer_5_out1, div, divu, En_Hi, En_Lo, Enable, EnableSP, EnableSP0, End,
       halt, j, jr, K_Selector, kbd, lw, mfhi, mflo, mult, mulu, N, nop, \nor , \or , or_26_out, or_27_out,
       ori, pop, push, Ready, rnd, RW0, RW1, S0, S1, S1_Beq, S1_Bgtz, S1_Blez, S1_Bltz, S1_Bne, SA0, SA1,
       SA2, SA2_Beq, SA2_Bne, SA3, SD0, SD0_Pop, SD1, SD2, SelectorR, SLoHi, slt, slti, sltiu, sltu, START,
       START_INSTRUCTION, sub, sw, tty, \xor , xori;
  wire [1:0] SMASK, SRAMA;
  wire [3:0] RAM_MASK0, RAM_MASK1, RAM_MASKPop, RAM_MASKPush, RAM_MASKSw;
  wire [4:0] RD, RS, RT;
  wire [5:0] Funtion_Code, Operation_Code;
  wire [15:0] K, RAM_A0, RAM_A1, RAM_APop, RAM_APush, RAM_ASw;
  wire [25:0] Destino_Salto;
  wire [31:0] bcu_1_out_9, bit_extender_1_out, K_ext_0, K_ext_last_bit, main_2_instruction_code,
       multiplexer_1_out, multiplexer_2_out, multiplexer_3_out, Out_ALU, Out_HI, Out_Hi_t, Out_LO, Out_Lo_t,
       Out_RT, Out_SP, Out_SP_4, Out_SP_4_t, RAM, RAM_INPUT_0_Push, RAM_INPUT_0_Sw, RAM_INPUT_1_Push,
       RAM_INPUT_1_Sw, RAM_INPUT_2_Push, RAM_INPUT_2_Sw, RAM_INPUT_3_Push, RAM_INPUT_3_Sw, RAM_Lw,
       RAM_OUTPUT_0_Lw, RAM_OUTPUT_0_Pop, RAM_OUTPUT_1_Lw, RAM_OUTPUT_1_Pop, RAM_OUTPUT_2_Lw,
       RAM_OUTPUT_2_Pop, RAM_OUTPUT_3_Lw, RAM_OUTPUT_3_Pop, RAM_Pop, RANDOM, register_1_q;
  wire [31:7] Out_RS;

  and and_1 (Cont_Nop, nop, START_INSTRUCTION);
  and and_2 (Cont_Add, add, START_INSTRUCTION);
  and and_3 (Cont_Sub, sub, START_INSTRUCTION);
  and and_4 (Cont_Mult, mult, START_INSTRUCTION);
  and and_5 (Cont_Mulu, mulu, START_INSTRUCTION);
  and and_6 (Cont_Divu, divu, START_INSTRUCTION);
  and and_7 (Cont_Div, div, START_INSTRUCTION);
  and and_8 (Cont_And, \and , START_INSTRUCTION);
  and and_9 (Cont_Or, \or , START_INSTRUCTION);
  and and_10 (Cont_Xor, \xor , START_INSTRUCTION);
  and and_11 (Cont_Nor, \nor , START_INSTRUCTION);
  and and_12 (BSelector_Addi, addi, START_INSTRUCTION);
  and and_13 (Cont_Slt, slt, START_INSTRUCTION);
  and and_14 (BSelector_Slti, slti, START_INSTRUCTION);
  and and_15 (BSelector_Sltiu, sltiu, START_INSTRUCTION);
  and and_16 (BSelector_Sltu, sltu, START_INSTRUCTION);
  and and_17 (BSelector_Andi, andi, START_INSTRUCTION);
  and and_18 (BSelector_Ori, ori, START_INSTRUCTION);
  and and_19 (BSelector_Xori, xori, START_INSTRUCTION);
  and and_20 (Kbd_Enable, kbd, START_INSTRUCTION);
  and and_21 (Cont_Rnd, rnd, START_INSTRUCTION);
  and and_22 (Stop, halt, START_INSTRUCTION);
  and and_23 (TTY_Enable, tty, START_INSTRUCTION);
  and and_24 (Cont_Mfhi, mfhi, START_INSTRUCTION);
  and and_25 (Cont_Mflo, mflo, START_INSTRUCTION);
  and and_26 (SA2_Beq, beq, START_INSTRUCTION);
  and and_27 (SA2_Bne, bne, START_INSTRUCTION);
  Demultiplexer #(.enable("false")) demultiplexer_1 (
    .out0(S1_Blez), .out1(demultiplexer_1_out1), .in(and_28_out), .sel(A_0_t_t));
  and and_28 (and_28_out, blez, START_INSTRUCTION);
  and and_29 (and_29_out, bgtz, START_INSTRUCTION);
  Demultiplexer #(.enable("false")) demultiplexer_2 (
    .out0(demultiplexer_2_out0), .out1(S1_Bgtz), .in(and_29_out), .sel(A_0_t_t));
  Demultiplexer #(.enable("false")) demultiplexer_3 (
    .out0(demultiplexer_3_out0), .out1(S1_Bltz), .in(and_30_out), .sel(A_0));
  and and_30 (and_30_out, bltz, START_INSTRUCTION);
  and and_31 (Cont_J, j, START_INSTRUCTION);
  and and_32 (Cont_Jr, jr, START_INSTRUCTION);
  Demultiplexer #(.enable("false")) demultiplexer_4 (
    .out0(demultiplexer_4_out0), .out1(S1_Beq), .in(SA2_Beq), .sel(Out_ALU[0]));
  Demultiplexer #(.enable("false")) demultiplexer_5 (
    .out0(S1_Bne), .out1(demultiplexer_5_out1), .in(SA2_Bne), .sel(Out_ALU[0]));
  or or_1 (Cont_Blez, S1_Blez, demultiplexer_1_out1);
  or or_2 (Cont_Bgtz, demultiplexer_2_out0, S1_Bgtz);
  or or_3 (Cont_Bltz, demultiplexer_3_out0, S1_Bltz);
  or or_4 (Cont_Beq, demultiplexer_4_out0, S1_Beq);
  or or_5 (Cont_Bne, S1_Bne, demultiplexer_5_out1);
  RegisterFile registerfile_1 (
    .in_1(Out_ALU), .out_24({Out_RS, TTY_ASCII_Data}), .out_25(Out_RT), .in_7(Clock), .in_8(Reset),
    .in_9(Enable), .in_15(RS), .in_16(RT), .in_10(En_Hi), .in_11(En_Lo), .in_12(SD0), .in_13(SD1),
    .in_14(SD2), .in_4(RAM), .in_5(Out_Hi_t), .in_6(Out_Lo_t), .in_2(Out_SP_4_t), .in_3(Out_SP_4),
    .in_18(SelectorR), .in_17(RD), .out_28(Out_HI), .out_29(Out_LO), .out_30(Out_SP), .in_19(EnableSP0),
    .in_20(Cont_Push), .out_26(Out_SP_4), .out_27(Out_SP_4_t), .in_21(EnableSP), .in_22(multiplexer_1_out),
    .in_23(RANDOM));
  Multiplexer #(.width(32), .enable("false")) multiplexer_1 (
    .in0({32{1'b1}}), .in1(bit_extender_1_out), .out(multiplexer_1_out), .sel(Kbd_Available));
  assign bit_extender_1_out = {{25{1'b0}}, Kbd_ASCII_Data};  // Bit_Extender bit_extender_1
  or or_6 (EnableSP, EnableSP0, Cont_Push);
  or or_7 (SLoHi, Cont_Mult, Cont_Mulu);
  and and_33 (EnableSP0, pop, START_INSTRUCTION);
  or or_8 (SA0, Cont_Sub, Cont_Div, Cont_Divu, Cont_And, Cont_Xor, BSelector_Andi, BSelector_Xori);
  or or_9 (SA1, Cont_Mult, Cont_Div, Cont_Divu, Cont_And, Cont_Nor, BSelector_Andi, Cont_Slt, BSelector_Sltu, BSelector_Slti, BSelector_Sltiu, Cont_Mulu);
  or or_10 (SA2, SA2_Beq, Cont_And, Cont_Slt, BSelector_Sltu, BSelector_Slti, BSelector_Sltiu, BSelector_Andi, SA2_Bne);
  or or_11 (SA3, Cont_Or, Cont_Xor, Cont_Nor, BSelector_Ori, BSelector_Xori);
  or or_12 (S1, S1_Beq, S1_Bne, S1_Blez, Cont_Jr, S1_Bgtz, S1_Bltz);
  or or_13 (S0, Cont_J, Cont_Jr);
  or or_14 (SelectorR, BSelector_Addi, BSelector_Slti, BSelector_Sltiu, BSelector_Andi, BSelector_Ori, BSelector_Xori, Cont_Lw);
  or or_15 (N, Cont_Mulu, Cont_Divu, BSelector_Sltu, BSelector_Sltiu);
  or or_16 (En_Hi, Cont_Mulu, Cont_Divu, Cont_Mult, Cont_Div);
  or or_17 (En_Lo, Cont_Mulu, Cont_Divu, Cont_Mult, Cont_Div);
  or or_18 (K_Selector, BSelector_Xori, BSelector_Sltiu, BSelector_Slti, BSelector_Ori);
  or or_19 (B_Selector, BSelector_Xori, BSelector_Andi, BSelector_Addi, BSelector_Sltu, BSelector_Slti, BSelector_Sltiu, BSelector_Lw, BSelector_Sw, BSelector_Ori);
  or or_20 (SD0, SD0_Pop, Cont_Lw, Cont_Mfhi, Kbd_Enable);
  or or_21 (SD1, Cont_Rnd, Cont_Mfhi, Cont_Mflo, Kbd_Enable);
  or or_22 (SD2, Kbd_Enable, Cont_Rnd, EnableSP0);
  BCU bcu_1 (
    .in_1(Clock), .in_2(Reset), .in_3(Cont), .in_4(S0), .in_5(S1), .out_9(bcu_1_out_9), .in_7(K),
    .in_8(Destino_Salto), .in_6({Out_RS, TTY_ASCII_Data}));
  or or_23 (SD0_Pop, EnableSP0, Cont_Pop);
  D_Flip_Flop u_START (.clk(Clock), .D(End), .Q(START), .preset(Reset));  // open: Qn, en, reset
  or or_24 (BSelector_Lw, BSelector_Lw0, BSelector_Lw1);
  Random #(.width(32)) random_1 (.clk(Clock), .next(START), .out(RANDOM));  // open: clr
  and and_34 (BSelector_Lw0, lw, START_INSTRUCTION);
  D_Flip_Flop START_2 (.clk(Clock), .D(Ready), .Q(START_INSTRUCTION), .reset(Reset));  // open: Qn, preset, en
  Multiplexer #(.width(32), .enable("false")) multiplexer_2 (
    .in0(K_ext_last_bit), .in1(K_ext_0), .out(multiplexer_2_out), .sel(K_Selector));
  or or_25 (Enable, Cont_Rnd, Cont_Add, Cont_Sub, Cont_And, Cont_Or, Cont_Xor, Cont_Nor, BSelector_Addi, Cont_Slt, BSelector_Sltu, BSelector_Slti, BSelector_Sltiu, BSelector_Andi, BSelector_Ori, BSelector_Xori, Cont_Lw, Cont_Pop, Cont_Mfhi, Cont_Mflo, Kbd_Enable);
  From_Ram_main main_1 (
    .Direccion(Out_SP_4_t), .CLK(Clock), .RT(Read_Time), .START(EnableSP0), .Banco_0(RAM_OUTPUT_0_Pop),
    .Banco_1(RAM_OUTPUT_1_Pop), .Banco_2(RAM_OUTPUT_2_Pop), .Banco_3(RAM_OUTPUT_3_Pop), .Address(RAM_APop),
    .MASK(RAM_MASKPop), .Ready(Cont_Pop), .Chip_Select(CS2), .Instruction_Code(RAM_Pop), .CLR(Reset));
  Multiplexer #(.width(32), .enable("false")) multiplexer_3 (
    .in0(Out_RT), .in1(multiplexer_2_out), .out(multiplexer_3_out), .sel(B_Selector));
  or or_26 (or_26_out, Cont_Add, Cont_Sub, Cont_Mult, Cont_Div, Cont_And, Cont_Or, Cont_Xor, Cont_Mulu, Cont_Divu, Cont_Nor, BSelector_Addi, Cont_Slt, BSelector_Sltu, BSelector_Slti, BSelector_Sltiu, BSelector_Andi, BSelector_Ori, BSelector_Xori, Cont_Lw, Cont_Sw, Cont_Pop, Cont_Push, Cont_Beq, Cont_Bne, Cont_Blez, Cont_Bgtz, Cont_Bltz, Cont_J, Cont_Jr, Cont_Mfhi, Cont_Mflo, Cont_Nop);
  or or_27 (or_27_out, Cont_Add, Cont_Sub, Cont_Mult, Cont_Div, Cont_And, Cont_Or, Cont_Xor, Cont_Mulu, Cont_Divu, Cont_Nor, BSelector_Addi, Cont_Slt, BSelector_Sltu, BSelector_Slti, BSelector_Sltiu, BSelector_Andi, BSelector_Ori, BSelector_Xori, Cont_Lw, Cont_Sw, Cont_Pop, Cont_Push, Cont_Beq, Cont_Bne, Cont_Blez, Cont_Bgtz, Cont_Bltz, Cont_J, Cont_Jr, Cont_Mfhi, Cont_Mflo, Cont_Nop);
  From_Ram_main main_2 (
    .Direccion(bcu_1_out_9), .CLK(Clock), .RT(Read_Time), .START(START), .Banco_0(RAM_Out_0),
    .Banco_1(RAM_Out_1), .Banco_2(RAM_Out_2), .Banco_3(RAM_Out_3), .Address(RAM_A0), .MASK(RAM_MASK0),
    .Ready(Ready), .Chip_Select(CS0), .Instruction_Code(main_2_instruction_code), .CLR(Reset));
  From_Ram_main main_3 (
    .Direccion(Out_ALU), .CLK(Clock), .RT(Read_Time), .START(BSelector_Lw0), .Banco_0(RAM_OUTPUT_0_Lw),
    .Banco_1(RAM_OUTPUT_1_Lw), .Banco_2(RAM_OUTPUT_2_Lw), .Banco_3(RAM_OUTPUT_3_Lw), .Address(RAM_A1),
    .MASK(RAM_MASK1), .Ready(Cont_Lw), .Chip_Select(BSelector_Lw1), .Instruction_Code(RAM_Lw), .CLR(Reset));
  ALU alu_1 (
    .in_1(N), .out_9(Out_Hi_t), .out_10(Out_ALU), .in_2({Out_RS, TTY_ASCII_Data}), .out_11(Out_Lo_t),
    .in_3(multiplexer_3_out), .in_4(SA0), .in_5(SA1), .in_6(SA2), .in_7(SA3), .out_12(A_0_t_t),
    .out_13(A_0_t), .out_14(A_0), .in_8(SLoHi));
  or or_28 (End, TTY_Enable, Kbd_Enable, Cont_Rnd, or_26_out);
  or or_29 (Cont, TTY_Enable, Kbd_Enable, Cont_Rnd, or_27_out);
  // Probe on main_2_instruction_code
  // Probe on RAM_Lw
  Register #(.width(32)) register_1 (
    .D(main_2_instruction_code), .en(Ready), .Q(register_1_q), .clk(Clock), .clr(Reset));
  Multiplexer #(.width(32), .enable("false")) multiplexer_4 (.in0(RAM_Lw), .in1(RAM_Pop), .out(RAM), .sel(Cont_Pop));
  Instruction_Decoder instruction_decoder_1 (
    .Instruction_Code(register_1_q), .ADD(add), .SUB(sub), .LW(lw), .AND(\and ), .OR(\or ), .NOT(\nor ),
    .XOR(\xor ), .SLT(slt), .Funct_Code(Funtion_Code), .SW(sltu), .K(K), .SLTU(sw), .POP(pop), .RD(RD),
    .TTY(tty), .PUSH(push), .RND(rnd), .Destino_Salto(Destino_Salto), .BLTZ(bltz), .J(j), .RT(RT), .BEQ(beq),
    .BNE(bne), .RS(RS), .BLEZ(blez), .BGTZ(bgtz), .JR(jr), .SLTI(slti), .SLTIU(sltiu), .ANDI(andi),
    .ADDI(addi), .ORI(ori), .XORI(xori), .MFHI(mfhi), .MFLO(mflo), .MULT(mult), .MULU(mulu), .DIV(div),
    .DIVU(divu), .NOP(nop), .HALT(halt), .OP_Code(Operation_Code), .KBD(kbd));
  // Probe on RT
  // Probe on RD
  // Probe on RS
  or or_30 (Chip_Select, CS0, BSelector_Lw1, CS2, BSelector_Sw1, CS4);
  // Probe on K
  assign K_ext_0 = {{16{1'b0}}, K};  // Bit_Extender bit_extender_2
  assign K_ext_last_bit = {{16{K[15]}}, K};  // Bit_Extender bit_extender_3
  or or_31 (SRAMA[0], BSelector_Sw1, BSelector_Lw1);
  or or_32 (SRAMA[1], BSelector_Sw1, CS2);
  or or_33 (SMASK[0], BSelector_Lw1, BSelector_Sw1);
  or or_34 (SMASK[1], CS2, BSelector_Sw1);
  Multiplexer #(.select(3), .width(16), .enable("false")) multiplexer_5 (
    .in0(RAM_A0), .in1(RAM_A1), .in2(RAM_APop), .in3(RAM_ASw), .in4(RAM_APush), .out(Address),
    .sel({CS4, SRAMA}));  // open: in5, in6, in7
  Multiplexer #(.select(3), .width(4), .enable("false")) multiplexer_6 (
    .in0(RAM_MASK0), .in1(RAM_MASK1), .in2(RAM_MASKPop), .in3(RAM_MASKSw), .in4(RAM_MASKPush), .out(Mask),
    .sel({CS4, SMASK}));  // open: in5, in6, in7
  and and_35 (BSelector_Sw0, sw, START_INSTRUCTION);
  or or_35 (BSelector_Sw, BSelector_Sw0, BSelector_Sw1);
  and and_36 (and_36_out, push, START_INSTRUCTION);
  WriteRam writeram_1 (
    .CLK(Clock), .CLR(Reset), .WT(Write_Time), .Direccion(Out_ALU), .START(BSelector_Sw0), .Input(Out_RT),
    .Address(RAM_ASw), .MASK(RAM_MASKSw), .Ready(Cont_Sw), .Bank_0(RAM_INPUT_0_Sw), .Bank_1(RAM_INPUT_1_Sw),
    .Bank_2(RAM_INPUT_2_Sw), .Bank_3(RAM_INPUT_3_Sw), .RW(RW0), .Chip_Select(BSelector_Sw1));
  WriteRam writeram_2 (
    .CLK(Clock), .CLR(Reset), .WT(Write_Time), .Direccion(Out_SP_4_t), .START(and_36_out),
    .Input({Out_RS, TTY_ASCII_Data}), .Address(RAM_APush), .MASK(RAM_MASKPush), .Ready(Cont_Push),
    .Bank_0(RAM_INPUT_0_Push), .Bank_1(RAM_INPUT_1_Push), .Bank_2(RAM_INPUT_2_Push),
    .Bank_3(RAM_INPUT_3_Push), .RW(RW1), .Chip_Select(CS4));
  or or_36 (nRead_Write, RW0, RW1);
  Demultiplexer #(.width(32), .enable("false")) demultiplexer_6 (
    .out0(RAM_OUTPUT_0_Lw), .out1(RAM_OUTPUT_0_Pop), .in(RAM_Out_0), .sel(CS2));
  Demultiplexer #(.width(32), .enable("false")) demultiplexer_7 (
    .out0(RAM_OUTPUT_1_Lw), .out1(RAM_OUTPUT_1_Pop), .in(RAM_Out_1), .sel(CS2));
  Demultiplexer #(.width(32), .enable("false")) demultiplexer_8 (
    .out0(RAM_OUTPUT_2_Lw), .out1(RAM_OUTPUT_2_Pop), .in(RAM_Out_2), .sel(CS2));
  Demultiplexer #(.width(32), .enable("false")) demultiplexer_9 (
    .out0(RAM_OUTPUT_3_Lw), .out1(RAM_OUTPUT_3_Pop), .in(RAM_Out_3), .sel(CS2));
  Multiplexer #(.width(32), .enable("false")) multiplexer_7 (
    .in0(RAM_INPUT_0_Sw), .in1(RAM_INPUT_0_Push), .out(RAM_In_0), .sel(CS4));
  Multiplexer #(.width(32), .enable("false")) multiplexer_8 (
    .in0(RAM_INPUT_1_Sw), .in1(RAM_INPUT_1_Push), .out(RAM_In_1), .sel(CS4));
  Multiplexer #(.width(32), .enable("false")) multiplexer_9 (
    .in0(RAM_INPUT_2_Sw), .in1(RAM_INPUT_2_Push), .out(RAM_In_2), .sel(CS4));
  Multiplexer #(.width(32), .enable("false")) multiplexer_10 (
    .in0(RAM_INPUT_3_Sw), .in1(RAM_INPUT_3_Push), .out(RAM_In_3), .sel(CS4));

  assign Kbd_Clear = Reset;

  // Other names for the same wires on the sheet: CLK = Clock; CS = Chip_Select; Enable_Add = Cont_Add;
  //   End_Add = Cont_Add; End_Beq = Cont_Beq; End_Bgtz = Cont_Bgtz; End_Blez = Cont_Blez; End_Bltz = Cont_Bltz;
  //   End_Bne = Cont_Bne; End_Nop = Cont_Nop; End_Sw = Cont_Sw; Cont_Tty = TTY_Enable; End_Tty = TTY_Enable;
  //   KBD_AVAIL = Kbd_Available; CLR = Reset; KBD_CLR = Reset; KBD_DATA[6:0] = Kbd_ASCII_Data;
  //   Out_RS[6:0] = TTY_ASCII_Data; TTY_DATA[6:0] = TTY_ASCII_Data; RAM_A[15:0] = Address;
  //   RAM_INPUT_0[31:0] = RAM_In_0; RAM_INPUT_1[31:0] = RAM_In_1; RAM_INPUT_2[31:0] = RAM_In_2;
  //   RAM_INPUT_3[31:0] = RAM_In_3; RAM_MASK[3:0] = Mask; RAM_OUTPUT_0[31:0] = RAM_Out_0;
  //   RAM_OUTPUT_1[31:0] = RAM_Out_1; RAM_OUTPUT_2[31:0] = RAM_Out_2; RAM_OUTPUT_3[31:0] = RAM_Out_3;
  //   RW = nRead_Write; End_J = Cont_J; S0_J = Cont_J; End_Jr = Cont_Jr; S0_Jr = Cont_Jr; S1_Jr = Cont_Jr;
  //   EnableSP1 = Cont_Push; End_Push = Cont_Push; S1SP = Cont_Push; Enable_Sub = Cont_Sub; End_Sub = Cont_Sub;
  //   SA0_Sub = Cont_Sub; En_Hi_Div = Cont_Div; En_Lo_Div = Cont_Div; End_Div = Cont_Div; N_Div = Cont_Div;
  //   SA0_Div = Cont_Div; SA1_Div = Cont_Div; En_Hi_Divu = Cont_Divu; En_Lo_Divu = Cont_Divu; End_Divu = Cont_Divu;
  //   N_Divu = Cont_Divu; SA0_Divu = Cont_Divu; SA1_Divu = Cont_Divu; Enable_And = Cont_And; End_And = Cont_And;
  //   SA0_And = Cont_And; SA1_And = Cont_And; SA2_And = Cont_And; Enable_Slt = Cont_Slt; End_Slt = Cont_Slt;
  //   SA1_Slt = Cont_Slt; SA2_Slt = Cont_Slt; Enable_Nor = Cont_Nor; End_Nor = Cont_Nor; SA1_Nor = Cont_Nor;
  //   SA3_Nor = Cont_Nor; Enable_Or = Cont_Or; End_Or = Cont_Or; SA3_Or = Cont_Or; Enable_Xor = Cont_Xor;
  //   End_Xor = Cont_Xor; SA0_Xor = Cont_Xor; SA3_Xor = Cont_Xor; Enable_Mfhi = Cont_Mfhi; End_Mfhi = Cont_Mfhi;
  //   SD0_Mfhi = Cont_Mfhi; SD1_Mfhi = Cont_Mfhi; Enable_Mflo = Cont_Mflo; End_Mflo = Cont_Mflo; SD1_Mflo = Cont_Mflo;
  //   Cont_Kbd = Kbd_Enable; Enable_Kbd = Kbd_Enable; End_Kbd = Kbd_Enable; SD0_Kbd = Kbd_Enable;
  //   SD1_Kbd = Kbd_Enable; SD2_Kbd = Kbd_Enable; S0SP = EnableSP0; SD0_Pop0 = EnableSP0; SD2_Pop = EnableSP0;
  //   Enable_Rnd = Cont_Rnd; End_Rnd = Cont_Rnd; SD1_Rnd = Cont_Rnd; SD2_Rnd = Cont_Rnd; Cont_Addi = BSelector_Addi;
  //   Enable_Addi = BSelector_Addi; End_Addi = BSelector_Addi; SelectorR_Addi = BSelector_Addi;
  //   Cont_Andi = BSelector_Andi; Enable_Andi = BSelector_Andi; End_Andi = BSelector_Andi;
  //   KSelector_Andi = BSelector_Andi; SA0_Andi = BSelector_Andi; SA1_Andi = BSelector_Andi;
  //   SA2_Andi = BSelector_Andi; SelectorR_Andi = BSelector_Andi; Enable_Lw = Cont_Lw; End_Lw = Cont_Lw;
  //   SD0_Lw = Cont_Lw; SelectorR_Lw = Cont_Lw; Cont_Ori = BSelector_Ori; Enable_Ori = BSelector_Ori;
  //   End_Ori = BSelector_Ori; KSelector_Ori = BSelector_Ori; SA3_Ori = BSelector_Ori; SelectorR_Ori = BSelector_Ori;
  //   Cont_Slti = BSelector_Slti; Enable_Slti = BSelector_Slti; End_Slti = BSelector_Slti;
  //   KSelector_Slti = BSelector_Slti; SA1_Slti = BSelector_Slti; SA2_Slti = BSelector_Slti;
  //   SelectorR_Slti = BSelector_Slti; Cont_Sltiu = BSelector_Sltiu; Enable_Sltiu = BSelector_Sltiu;
  //   End_Sltiu = BSelector_Sltiu; KSelector_Sltiu = BSelector_Sltiu; N_Sltiu = BSelector_Sltiu;
  //   SA1_Sltiu = BSelector_Sltiu; SA2_Sltiu = BSelector_Sltiu; SelectorR_Sltiu = BSelector_Sltiu;
  //   Cont_Sltu = BSelector_Sltu; Enable_Sltu = BSelector_Sltu; End_Sltu = BSelector_Sltu; N_Sltu = BSelector_Sltu;
  //   SA1_Sltu = BSelector_Sltu; SA2_Sltu = BSelector_Sltu; SelectorR_Sltu = BSelector_Sltu;
  //   Cont_Xori = BSelector_Xori; Enable_Xori = BSelector_Xori; End_Xori = BSelector_Xori;
  //   KSelector_Xori = BSelector_Xori; SA0_Xori = BSelector_Xori; SA3_Xori = BSelector_Xori;
  //   SelectorR_Xori = BSelector_Xori; En_Hi_Mult = Cont_Mult; En_Lo_Mult = Cont_Mult; End_Mult = Cont_Mult;
  //   SA1_Mult = Cont_Mult; SLoHi_Mult = Cont_Mult; En_Hi_Mulu = Cont_Mulu; En_Lo_Mulu = Cont_Mulu;
  //   End_Mulu = Cont_Mulu; N_Mulu = Cont_Mulu; SA1_Mulu = Cont_Mulu; SLoHi_Mulu = Cont_Mulu; SMASK[2] = CS4;
  //   SMASK2 = CS4; SRAMA[2] = CS4; SRAMA2 = CS4; SRAMIN = CS4; Enable_Pop = Cont_Pop; End_Pop = Cont_Pop;
  //   SD0_Pop1 = Cont_Pop; SRAM = Cont_Pop; CS1 = BSelector_Lw1; SMASK0Lw = BSelector_Lw1; SRAMA0Lw = BSelector_Lw1;
  //   CS3 = BSelector_Sw1; SMASK0Sw = BSelector_Sw1; SMASK1Sw = BSelector_Sw1; SRAMA0Sw = BSelector_Sw1;
  //   SRAMA1Sw = BSelector_Sw1; SMASK1Pop = CS2; SRAMA1Pop = CS2; SRAMOUT = CS2

  // Notes on the sheet:
  //   RAM ADDRESS
  //   DATA FROM RAM
  //   DATA TO RAM
  //   DATA WRITE MASK
  //   RAM TIMING
  //   RAM CONTROL
  //   KEYBOARD
  //   TTY
  //   SEQUENCING
endmodule

module DemultiplexerBancos (
  input  [31:0] INPUT,
  input  [3:0] MASK,
  output [31:0] Bank_0,
  output [31:0] Bank_1,
  output [31:0] Bank_2,
  output [31:0] Bank_3
);

  Transistor #(.\type ("n"), .gate("br"), .width(32)) transistor_1 (.in(INPUT), .out(Bank_0), .gate(MASK[0]));
  Transistor #(.\type ("n"), .gate("br"), .width(32)) transistor_2 (.in(INPUT), .out(Bank_1), .gate(MASK[1]));
  Transistor #(.\type ("n"), .gate("br"), .width(32)) transistor_3 (.in(INPUT), .out(Bank_2), .gate(MASK[2]));
  Transistor #(.\type ("n"), .gate("br"), .width(32)) transistor_4 (.in(INPUT), .out(Bank_3), .gate(MASK[3]));
endmodule

module WriteRam (
  input  CLK,
  input  CLR,
  input  [3:0] WT,
  input  [31:0] Direccion,
  input  START,
  input  [31:0] Input,
  output [15:0] Address,
  output [3:0] MASK,
  output RW,
  output Ready,
  output Chip_Select,
  output [31:0] Bank_0,
  output [31:0] Bank_1,
  output [31:0] Bank_2,
  output [31:0] Bank_3
);

  wire demultiplexer_2_out0, \end , Load, or_1_out;
  wire [31:0] little_endian_1_out;

  Counter #(.width(4), .max('hf)) counter_1 (
    .load(Load), .D(WT), .count(Chip_Select), .carry(\end ), .clk(CLK));  // open: Q, clr
  or or_1 (or_1_out, demultiplexer_2_out0, START);
  Little_Endian little_endian_1 (.IN(Input), .OUT(little_endian_1_out));
  D_Flip_Flop d_ff_1 (.clk(CLK), .D(or_1_out), .Q(Chip_Select), .reset(CLR));  // open: Qn, preset, en
  Demultiplexer #(.select(2), .width(32), .enable("false")) demultiplexer_1 (
    .out0(Bank_0), .out1(Bank_1), .out2(Bank_2), .out3(Bank_3), .in(little_endian_1_out), .sel(Direccion[3:2]));
  or or_2 (Load, START, Chip_Select);
  Shifter #(.width(4)) shifter_1 (.in(4'b0001), .\dist (Direccion[3:2]), .out(MASK));
  Demultiplexer demultiplexer_2 (.out0(demultiplexer_2_out0), .out1(Ready), .in(Chip_Select), .sel(\end ));  // open: en

  assign Address = Direccion[19:4];
  assign RW = Chip_Select;

  // Other names for the same wires on the sheet: Selector[1:0] = Direccion[3:2]; Load1 = START; Count = Chip_Select;
  //   Load2 = Chip_Select
endmodule
